# Fritzing sketch Esp8266 (saved by Fritzing 0.9.3b)
breadboards: 1

parts:
  R1 = Resistor [tolerance=±5% resistance=110 package=THT]
  U1 = Optocoupler [package=THT]
  Q1 = Basic FET N-Channel [package="D2Pak [SMD]"]
  R2 = Resistor [tolerance=±5% resistance=10k package=THT]
  70v = Power plug
  5V = Power plug
  U2 = NodeMCU V1.0
  M1 = DC Motor

nets:
  N1: R1.Pin_0, U1.Pin_1
  N2: R1.Pin_1, U2.D1
  N3: U1.Pin_2, U2.GND
  GND: U1.Pin_4, 70v.GND, 5V.GND, M1.pin_2
  N4: U1.Pin_5, Q1.Gate, R2.Pin_1
  N5: Q1.drain, 70v.VCC
  N6: Q1.source, M1.pin_1
  N7: R2.Pin_0, 5V.VCC

custom parts:
  NodeMCU V1.0: ESP8266 based NodeMCU
